# Fritzing sketch arduinoSchematic (saved by Fritzing 0.9.3b)

parts:
  Part1 = Adafruit Bluefruit LE Shield [part_number="Adafruit #2746"]  # not connected
  Part2 = Arduino Uno (Rev3) - ICSP  # not connected
  Part3 = Adafruit PowerBoost 500 Shield [part_number="Adafruit #2078"]  # not connected
  U1 = LIPO-2000mAh [package=lipo-2000]  # not connected
  Part4 = Adafruit Proto Shield R3 [part_number="Adafruit #2077"]
  R1 = Basic Flex Resistor
  R2 = Resistor [tolerance=±5% resistance=10k package=THT]

nets:
  N1: Part4.+5V, Part4.N$271
  N2: Part4.A0, Part4.N$36
  N3: Part4.GND, Part4.N$27
  N4: Part4.N$21, R1.pin_1
  N5: Part4.N$26, R2.Pin_0
  N6: Part4.N$49, R1.Pin_2
  N7: Part4.N$87, R2.Pin_1

custom parts:
  Adafruit Bluefruit LE Shield: Would you like to add powerful and easy-to-use Bluetooth Low Energy to your robot, art or other electronics project? Heck yeah! With BLE now included in modern smart phones and tablets, its fun to add wireless connectivity. So what you really need is the new Adafruit Bluefruit LE Shield for Arduino! The Bluefruit LE Shield makes it easy to add Bluetooth Low Energy connectivity to your Arduino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
  Adafruit PowerBoost 500 Shield: What's a project if it's trapped on your desk? Now you can take your Arduino anywhere you wish with the PowerBoost shield! This stackable shield goes onto your Arduino and provides a slim rechargeable power pack, with a built in battery charger as well as DC/DC booster. Compatible with Arduino Uno, Duemilanove, Mega, Leonardo and Due - basically any Arduino-pinout-shaped Arduino as only the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
  Adafruit Proto Shield R3: This prototyping shield is the best out there (well, we think so, at least), and now is even better with Version R3 - updated for the most compatibility with just about all the Arduinos! It works with UNO, Mega, Leonardo, NG, Diecimila, Duemilanove, and compatible Arduinos. Yun's and Arduino Ethernets have a chunky Ethernet jack that gets in the way of stacking, you can use the stacking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
