# Fritzing sketch standaloneCircuitSchematic (saved by Fritzing 0.9.3b)
breadboards: 1

parts:
  R1 = Resistor [tolerance=±5% resistance=10k package=THT]
  C1 = Ceramic Capacitor [capacitance=22pF package="100 mil [THT, multilayer]"]
  Xtal1 = CRYSTAL - kHz [frequency="16 Mhz"]
  C2 = Ceramic Capacitor [capacitance=22pF package="100 mil [THT, multilayer]"]
  R2 = Resistor [tolerance=±5% resistance=560 package=THT]
  LED1 = LED - 5mm [color="Red (633nm)" package="5 mm [THT]"]
  J1 = Screw terminal - 2 pins [package=THT]
  D1 = Rectifier Diode [part_number=1N5059 package="300 mil [THT]"]
  D2 = Rectifier Diode [part_number=1N5059 package="300 mil [THT]"]
  D3 = Rectifier Diode [part_number=1N5059 package="300 mil [THT]"]
  D4 = Rectifier Diode [part_number=1N5059 package="300 mil [THT]"]
  C3 = Electrolytic Capacitor [capacitance=1mF package="100 mil [THT, electrolytic]"]
  C4 = Ceramic Capacitor [capacitance=100nF package="100 mil [THT, multilayer]"]
  D5 = Rectifier Diode [part_number=1N4001 package="300 mil [THT]"]
  C5 = Electrolytic Capacitor [capacitance=1µF package="100 mil [THT, electrolytic]"]
  C6 = Ceramic Capacitor [capacitance=100nF package="100 mil [THT, multilayer]"]
  LED2 = LED - 5mm [color="Green (565nm)" package="5 mm [THT]"]
  R3 = Resistor [tolerance=±5% resistance=470 package=THT]
  IC1 = ATmega 328P [package=dip]
  IC2 = LM7805 [part_number=LM7805 package=TO-220]
  VCC1 = Battery block 9V
  R4 = Basic Flex Resistor [part_number=SEN-10264]
  R5 = Resistor [tolerance=±5% resistance=10k package=THT]
  IC3 = LM7805 [part_number=LM9805 package=TO-220]  # not connected
  Part1 = Adafruit Bluefruit LE UART Friend [part_number="Adafruit #2479"]

nets:
  VCC: R1.Pin_0, LED1.anode, D5.anode, C5.+, C6.0, LED2.anode, IC1.VCC, IC1.AVCC, IC2.OUT, R5.Pin_1, Part1.VIN
  N1: R1.Pin_1, IC1.PC6_(PCINT14/^RESET)_[RESET]
  GND: C1.0, C2.1, D3.anode, D4.anode, C3.-, C4.1, C5.-, C6.1, R3.Pin_1, IC1.GND, IC2.GND, R4.pin_1, Part1.GND
  N2: C1.1, Xtal1.pin_1, IC1.PB6_(PCINT6/XTAL1/TOSC1)_[XTAL1]
  N3: Xtal1.pin_0, C2.0, IC1.PB7_(PCINT7/XTAL2/TOSC2)_[XTAL2]
  N4: R2.Pin_0, IC1.PB5_(SCK/PCINT5)_[D13]
  N5: R2.Pin_1, LED1.cathode
  N6: J1.pin1, D2.anode, D4.cathode, VCC1.+
  N7: J1.pin2, D1.anode, D3.cathode, VCC1.-
  N8: D1.cathode, D2.cathode, C3.+, C4.0, D5.cathode, IC2.IN
  N9: LED2.cathode, R3.Pin_0
  N10: IC1.PB0_(PCINT0/CLK0/ICP1)_[D8], Part1.RTS
  N11: IC1.PB1_(OC1A/PCINT1)_[D9_PWM], Part1.RXI
  N12: IC1.PB2_(^SS/OC1B/PCINT2)_[D10_PWM], Part1.TXO
  N13: IC1.PB3_(MOSI/OC2A/PCINT3)_[D11_PWM], Part1.CTS
  N14: IC1.PB4_(MISO/PCINT4)_[D12], Part1.MODE
  N15: IC1.PC3_(ADC3/PCINT11)_[A3], R4.Pin_2, R5.Pin_0

custom parts:
  ATmega 328P: Atmel ATmega 328P-PU Microcontroller
  LM7805: LM 7805 Voltage Regulator
  Adafruit Bluefruit LE UART Friend: The Bluefruit LE UART Friend makes it easy to add Bluetooth Low Energy connectivity to anything with a hardware or software serial port. We even have nice hardware flow control so you won't have to think about losing data. Connect to your Arduino or other microcontroller or even just a standard FTDI cable for debugging and testing.
